# Fritzing sketch SOS Modified (saved by Fritzing 0.9.3b)
breadboards: 1

parts:
  U1 = NodeMCU V1.0
  LED1 = RGB LED (com. cathode, rbg) [package="5 mm [THT]"]
  R1 = Resistor [tolerance=±5% resistance=220 package="2010 [SMD]"]

nets:
  N1: U1.GND, LED1.common_cathode
  N2: U1.D6, R1.Pin_0
  N3: LED1.green_anode, R1.Pin_1

custom parts:
  NodeMCU V1.0: ESP8266 based NodeMCU
