# Fritzing sketch DHT & LED (saved by Fritzing 0.9.3b)
breadboards: 1

parts:
  U1 = NodeMCU V1.0
  LED1 = RGB LED - (4 legs) [package="5 mm [THT]"]
  DHT1 = DHT11 Humitidy and Temperature Sensor

nets:
  N1: U1.D0, DHT1.DATA
  N2: U1.D1, LED1.red_cathode
  N3: U1.D2, LED1.green_cathode
  N4: U1.D3, LED1.blue_cathode
  GND: U1.GND, LED1.common_anode, DHT1.GND
  VIN: U1.Vin, DHT1.VDD

custom parts:
  NodeMCU V1.0: ESP8266 based NodeMCU
  DHT11 Humitidy and Temperature Sensor: DHT11 Humidity and Temperature Sensor
