# Fritzing sketch LDR LED (saved by Fritzing 0.9.3b)
breadboards: 1

parts:
  U1 = NodeMCU V1.0
  e-radionica_com1 = LM393 LDR breakout [part_number=100027]
  LED1 = RGB LED (com. cathode, rgb) [package="5 mm [THT]"]

nets:
  N1: U1.D2, LED1.red_anode
  N2: U1.D3, LED1.green_anode
  N3: U1.D4, LED1.blue_anode
  GND: U1.GND, e-radionica_com1.GND, LED1.common_cathode
  N4: U1.A0, e-radionica_com1.AO

custom parts:
  NodeMCU V1.0: ESP8266 based NodeMCU
