# Fritzing sketch LCD DHT LED (saved by Fritzing 0.9.3b)
breadboards: 1

parts:
  U1 = NodeMCU V1.0
  DHT1 = DHT11 Humitidy and Temperature Sensor
  Part1 = LCD1602-I2C
  LED1 = RGB LED (com. cathode, rgb) [package="5 mm [THT]"]

nets:
  N1: U1.D1, DHT1.DATA, Part1.SCL
  N2: U1.D2, Part1.SDA
  N3: U1.D3, LED1.red_anode
  N4: U1.D4, LED1.green_anode
  GND: U1.GND, DHT1.NULL, Part1.GND, LED1.common_cathode
  N5: U1.D5, LED1.blue_anode
  VIN: U1.Vin, DHT1.VDD, Part1.VCC

custom parts:
  NodeMCU V1.0: ESP8266 based NodeMCU
  DHT11 Humitidy and Temperature Sensor: DHT11 Humidity and Temperature Sensor
  LCD1602-I2C: A standard character display, usually with 2x16 characters. Comes in many colors with LCM1602 IIC attached.
